# Fritzing sketch Salinan Sensor LDR Nodemcu (saved by Fritzing 0.9.5d)

parts:
  U1 = NodeMCU V1.0  # not connected
  LED1 = smd LED [color="Red (633nm)" package="0805 [SMD]"]
  e-radionica_com1 = LM393 LDR breakout [part_number=100027]  # not connected
  Mod1 = KY-019 5V Relay Module [package="Breakout board"]

nets:
  N1: LED1.anode, Mod1.Common

custom parts:
  NodeMCU V1.0: ESP8266 based NodeMCU
  KY-019 5V Relay Module: KY-019 5V Relay module, used to control AC circuits. (Special thanks to vanepp for fixing the PCB holes and other errors)
