# Fritzing sketch Skematik Rangkaian (saved by Fritzing 0.9.3b)

parts:
  NodeMCU_v1 = NodeMCU v3 LoLin [part_number=ESP8266]
  YL-83_-_Detection_Board1 = YL-83 Rain Sensor - Detection Board
  YL-83_-_Control_Board1 = YL-83 Rain Sensor - Control Board

nets:
  GND: NodeMCU_v1.GND, YL-83_-_Control_Board1.GND
  3V3: NodeMCU_v1.3V3, YL-83_-_Control_Board1.VCC
  N1: NodeMCU_v1.A0, YL-83_-_Control_Board1.AO
  N2: YL-83_-_Detection_Board1.POS, YL-83_-_Control_Board1.POS
  N3: YL-83_-_Detection_Board1.NEG, YL-83_-_Control_Board1.NEG

notes:
  BLINK

custom parts:
  NodeMCU v3 LoLin: NodeMCU v3 LoLin NodeMCU (http://www.nodemcu.com/) is an open source IoT platform. It includes firmware (https://nodemcu-build.com/) which runs on the ESP8266 Wi-Fi SoC from Espressif Systems, and hardware which is based on the ESP-12E module. The term "NodeMCU" by default refers to the firmware rather than the dev kits. The firmware uses the Lua scripting language. It is based on the eLua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
  YL-83 Rain Sensor - Detection Board: The YL-83 is a rain sensor that has more resistance when dry and less resistance when wet. The module runs at 5V.
  YL-83 Rain Sensor - Control Board: The YL-83 is a rain sensor that has more resistance when dry and less resistance when wet. The module runs at 5V.

// code stored in the sketch: Blink.ino
/*
  Blink
  
  Switching a LED on and off
  
  This example is part of the Fritzing Creator Kit: www.fritzing.org/creator-kit.
*/

int led = 13;                   // integer variable led is declared

void setup() {                  // the setup() method is executed only once
  pinMode(led, OUTPUT);         // the led PIN is declared as digital output
}

void loop() {                   // the loop() method is repeated
  digitalWrite(led, HIGH);      // switching on the led 
  delay(1000);                  // stopping the program for 1000 milliseconds
  digitalWrite(led, LOW);       // switching off the led 
  delay(1000);                  // stopping the program for 1000 milliseconds
}
